// Logisim project Q4B3.circ as structural Verilog: 1 circuit, main circuit main
module main (
  input  Reset,
  input  CLK,
  input  [7:0] Data_In,
  input  MemWrite,
  input  RAM_Reset,
  input  Mem_Read_Write,
  output MSB,
  output out_8,
  output out_9,
  output out_10,
  output out_11,
  output out_12,
  output out_13,
  output LSB
);

  wire [7:0] adder_1_out, and_1_out, register_1_q;

  assign and_1_out = adder_1_out & {8{Reset}};  // AND_Gate and_1, 8 bits wide
  Register register_1 (.D(and_1_out), .Q(register_1_q), .clk(CLK));  // open: en, clr
  assign {MSB, out_8, out_9, out_10, out_11, out_12, out_13, LSB} = Mem_Read_Write ? Data_In : 8'bz;  // Controlled_Buffer controlled_buffer_1
  Adder adder_1 (.a(register_1_q), .b(8'h1), .out(adder_1_out));  // open: cin, cout
  RAM ram_1 (
    .addr(register_1_q), .data({MSB, out_8, out_9, out_10, out_11, out_12, out_13, LSB}), .sel(1'b1),
    .clk(CLK), .ld(MemWrite), .clr(RAM_Reset));

  // Notes on the sheet:
  //   Address
  //   Data Out
endmodule
