// Logisim project 5.circ as structural Verilog: 2 circuits, main circuit main
module main (
);

  wire Control_alu, Control_memtoreg, Control_memwrite, Control_regdst, Control_regwrite;
  wire [1:0] Control_alu_op, INSTRUCTION_MEMORY_PC_msb, INSTRUCTION_MEMORY_PC_out_7,
       INSTRUCTION_MEMORY_PC_out_9, INSTRUCTION_MEMORY_PC_out_11, multiplexer_1_out;
  wire [3:0] ALU_output, DATA_MEM_REG_dataout, multiplexer_2_out, multiplexer_3_out, undriven, undriven_2;

  Q4B3_main INSTRUCTION_MEMORY_PC (
    .MSB(INSTRUCTION_MEMORY_PC_msb[0]), .out_6(INSTRUCTION_MEMORY_PC_msb[1]),
    .out_7(INSTRUCTION_MEMORY_PC_out_7[0]), .out_8(INSTRUCTION_MEMORY_PC_out_7[1]),
    .out_9(INSTRUCTION_MEMORY_PC_out_9[0]), .out_10(INSTRUCTION_MEMORY_PC_out_9[1]),
    .out_11(INSTRUCTION_MEMORY_PC_out_11[0]), .LSB(INSTRUCTION_MEMORY_PC_out_11[1]));  // open: Reset, Data_In, RAM_Reset, Mem_Read_Write
  Multiplexer #(.width(2), .enable("false")) multiplexer_1 (
    .in0(INSTRUCTION_MEMORY_PC_out_9), .in1(INSTRUCTION_MEMORY_PC_out_11), .out(multiplexer_1_out),
    .sel(Control_regdst));
  Multiplexer #(.width(4), .enable("false")) multiplexer_2 (
    .in0(ALU_output), .in1(DATA_MEM_REG_dataout), .out(multiplexer_2_out), .sel(Control_memtoreg));
  ControlTruth Control (
    .OpCode(INSTRUCTION_MEMORY_PC_msb), .RegDst(Control_regdst), .ALU(Control_alu),
    .MemtoReg(Control_memtoreg), .RegWrite(Control_regwrite), .MemWrite(Control_memwrite),
    .ALU_OP(Control_alu_op));  // open: MemRead
  ALU ALU (
    .Input1(undriven), .Input2(multiplexer_3_out), .ControlBits(Control_alu_op), .Output(ALU_output));  // open: CarryOut, Zero
  Multiplexer #(.width(4), .enable("false")) multiplexer_3 (
    .in0(undriven_2), .in1({INSTRUCTION_MEMORY_PC_out_11, 2'b00}), .out(multiplexer_3_out), .sel(Control_alu));
  Diarmuid_Ryan_11363776_A4_main DATA_MEM_REG (
    .RegOut1(undriven), .RegOut2(undriven_2), .RegRead1(INSTRUCTION_MEMORY_PC_out_7),
    .RegRead2(multiplexer_1_out), .RegWrite_2(Control_regwrite), .MemAdd(ALU_output),
    .MemWrite(Control_memwrite), .DataOut(DATA_MEM_REG_dataout), .WriteData(multiplexer_2_out));  // open: RegWrite, ExtDataWrite, ExtData, CLK

  // Notes on the sheet:
  //   OP
  //   RS
  //   RT
  //   RD/Offset
endmodule

module main2 (
  input  [7:0] DataIn
);

  wire Control_alu, Control_memtoreg, Control_memwrite, Control_regdst, Control_regwrite, not_1_out;
  wire [1:0] Control_alu_op, main_1_msb, main_1_out_7, main_1_out_9, main_1_out_11, multiplexer_1_out,
       multiplexer_2_out;
  wire [3:0] ALU_output, b_1_dataout, multiplexer_3_out, multiplexer_4_out, RegFile_readdata1,
       RegFile_readdata2;

  Q4B3_main main_1 (
    .Data_In(DataIn), .Mem_Read_Write(1'b1), .MSB(main_1_msb[0]), .out_6(main_1_msb[1]),
    .out_7(main_1_out_7[0]), .out_8(main_1_out_7[1]), .out_9(main_1_out_9[0]), .out_10(main_1_out_9[1]),
    .out_11(main_1_out_11[0]), .LSB(main_1_out_11[1]));  // open: Reset, RAM_Reset
  Multiplexer #(.width(2), .enable("false")) multiplexer_1 (
    .in0(main_1_out_9), .in1(main_1_out_11), .out(multiplexer_1_out), .sel(not_1_out));
  not not_1 (not_1_out, Control_regdst);
  Multiplexer #(.width(2), .enable("false")) multiplexer_2 (
    .in0(main_1_out_9), .in1(main_1_out_11), .out(multiplexer_2_out), .sel(Control_regdst));
  Multiplexer #(.width(4), .enable("false")) multiplexer_3 (
    .in0(ALU_output), .in1(b_1_dataout), .out(multiplexer_3_out), .sel(Control_memtoreg));
  reg_file RegFile (
    .WriteData(multiplexer_3_out), .WriteReg(multiplexer_1_out), .RegWrite(Control_regwrite),
    .ReadData1(RegFile_readdata1), .ReadReg1(main_1_out_7), .ReadData2(RegFile_readdata2),
    .ReadReg2(multiplexer_2_out));  // open: Clock
  ControlTruth Control (
    .OpCode(main_1_msb), .RegDst(Control_regdst), .ALU(Control_alu), .MemtoReg(Control_memtoreg),
    .RegWrite(Control_regwrite), .MemWrite(Control_memwrite), .ALU_OP(Control_alu_op));  // open: MemRead
  ALU ALU (
    .Input1(RegFile_readdata1), .Input2(multiplexer_4_out), .ControlBits(Control_alu_op), .Output(ALU_output));  // open: CarryOut, Zero
  Multiplexer #(.width(4), .enable("false")) multiplexer_4 (
    .in0(RegFile_readdata2), .in1({main_1_out_11, 2'b00}), .out(multiplexer_4_out), .sel(Control_alu));
  b b_1 (
    .Address(ALU_output), .DataLoad(RegFile_readdata2), .Store(Control_memwrite), .DataOut(b_1_dataout));  // open: Offset, CLK

  // Notes on the sheet:
  //   OP
  //   RS
  //   RT
  //   RD/Offset
endmodule
