// Logisim project ControlTruth.circ as structural Verilog
module ControlTruth (
  input  [1:0] OpCode,
  output RegDst,
  output ALU,
  output MemtoReg,
  output RegWrite,
  output MemRead,
  output MemWrite
);

  wire not_1_out, not_2_out;

  not not_1 (not_1_out, OpCode[1]);
  not not_2 (not_2_out, OpCode[1]);
  and and_1 (MemWrite, OpCode[0], OpCode[1]);
  or or_1 (ALU, not_1_out, OpCode[0]);
  and and_2 (MemRead, OpCode[0], not_2_out);
  // Probe on 2'b00

  assign MemtoReg = OpCode[0];
  assign RegDst = OpCode[1];
  assign RegWrite = 1'b1;
endmodule
